# Fritzing sketch teensy2 (saved by Fritzing 0.9.3b)
circuit board: 7.61cm x 5.06cm
breadboards: 1

parts:
  Teensy_2 = Teensy 2.0
  J4 = female pin header, 2 pins [form="♀ (female)"]
  J6 = female pin header, 2 pins [form="♀ (female)"]
  J1 = screw terminal, 12 pins
  J3 = screw terminal, 2 pins
  J7 = screw terminal, 2 pins
  J5 = male pin header, 12 pins [form="♂ (male)"]
  R1 = Resistor [tolerance=±5% resistance=220 package=THT]

nets:
  N1: Teensy_2.GND, J1.pin1, J1.pin2, J5.pin11, J5.pin12, R1.Pin_0
  N2: Teensy_2.B1, J6.pin2, J7.pin1
  N3: Teensy_2.B2, J1.pin12, J5.pin1
  N4: Teensy_2.B3, J1.pin11, J5.pin2
  N5: Teensy_2.B7, J1.pin10, J5.pin3
  N6: Teensy_2.D0, J1.pin9, J5.pin4
  N7: Teensy_2.D1, J1.pin8, J5.pin5
  N8: Teensy_2.D2, J1.pin7, J5.pin6
  N9: Teensy_2.D3, J1.pin6, J5.pin7
  N10: Teensy_2.C6, J1.pin5, J5.pin8
  N11: Teensy_2.C7, J1.pin4, J5.pin9
  N12: Teensy_2.VCC, J1.pin3, J5.pin10
  N13: J4.pin1, J3.pin2
  N14: J4.pin2, J3.pin1
  N15: J6.pin1, J7.pin2, R1.Pin_1

notes:
  Encoder A
  X
  Y
  Z
  A
  X1
  X10
  X100
  COM
  +5v
  Gnd
  Encoder B
  Vcc
  ESTOP
  ESTOP IN
  ESTOP OUT
  LED
